# Fritzing sketch PFFrizting (saved by Fritzing 0.9.3b)
breadboards: 1

parts:
  J1 = STM32 Nucleo boards
  LED1 = LED - 3mm [color="Red (633nm)" current=0.030 package="3 mm [THT]"]
  R4 = Resistor [tolerance=±5% resistance=68 package="2512 [SMD]"]
  M1 = DOIT Esp32 DevKit v1 (30 pins long, 11 pins width) [part_number=ESP32S-PIN30]
  hc-sr1 = hc-sr04
  Grove1 = Grove Light Sensor
  Grove2 = Grove Temperature Sensor
  Grove3 = Grove Buzz
  R5 = Rotary Potentiometer (Small) [maximum_resistance=100kΩ package=THT]
  J2 = Basic Servo
  LED2 = RGB LED (com. cathode, rbg) [package="5 mm [THT]"]

nets:
  N1: J1.A0, R5.leg2
  N2: J1.A1, J2.pulse
  N3: J1.A2, Grove2.SIG
  N4: J1.PC6, LED2.red_anode, LED2.blue_anode
  N5: J1.D8, M1.RX2
  N6: J1.D12/MISO, Grove1.SIG
  N7: J1.A4/SDA, LED2.green_anode
  N8: J1.D2, M1.TX2
  N9: J1.D5_PWM, hc-sr1.Trig, hc-sr1.Echo
  N10: J1.D7, R4.Pin_1
  VCC: J1.3V3, Grove3.VCC, J2.vcc
  VCC_2: J1.5V, hc-sr1.VCC, Grove1.VCC, Grove2.VCC, R5.wiper
  GND: J1.GND, LED1.cathode, hc-sr1.GND, Grove1.GND, Grove2.GND, R5.leg1, J2.gnd, LED2.common_cathode
  N11: LED1.anode, R4.Pin_0
  N12: M1.D23, Grove3.SIG
  GND_2: M1.GND, Grove3.GND

custom parts:
  DOIT Esp32 DevKit v1 (30 pins long, 11 pins width): The DOIT Esp32 DevKit v1 is one of the development board created by DOIT to evaluate the ESP-WROOM-32 module. It is based on the ESP32 microcontroller that boasts Wifi, Bluetooth, Ethernet and Low Power support all in a single chip. (vanepp) made breadboard work, adjusted pin numbering and labels and reduced size of schematic and cleaned up pcb. This chip is 30pins long (2 x15) and 11 pins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
